// Logisim project Logism.circ as structural Verilog: 1 circuit, main circuit main
module main (
  input  in_1,
  output out_2
);

  // Probe on nothing
  Multiplexer multiplexer_1 ();  // open: in0, in1, out, sel, en
  Demultiplexer demultiplexer_1 ();  // open: out0, out1, in, sel, en
  Decoder decoder_1 ();  // open: out0, out1, sel, en
  BitSelector bitselector_1 ();  // open: in, out, sel
  T_Flip_Flop t_ff_1 ();  // open: clk, T, Q, Qn, preset, reset, en
  Priority_Encoder priority_encoder_1 ();  // open: in0, in1, in2, in3, in4, in5, in6, in7, out, en_in, gs, en_out
  S_R_Flip_Flop s_r_ff_1 ();  // open: S, clk, R, Q, Qn, preset, reset, en
  D_Flip_Flop d_ff_1 ();  // open: clk, D, Q, Qn, preset, en, reset
  J_K_Flip_Flop j_k_ff_1 ();  // open: J, clk, K, Q, Qn, preset, en, reset

  // Notes on the sheet:
  //   Ele atua como um "distribuidor" de sinal.
  //   X: sinal indefinido, que indica um erro ou condição indefinida.
  //   Z: alta impedância, significa que o fio não está conectado a uma fonte ativa.
  //   Input Pin (Pino de Entrada): Um componente que injeta um valor digital no circuito (0 ou 1).
  //   Output Pin (Pino de Saída): Um pino que permite observar o valor resultante de um circuito.
  //   é um circuito ou operação que seleciona um ou mais bits de uma palavra de dados ou registro e os direciona para a saída.
  //   Muda de estado (0 para 1 ou 1 para 0) toda vez que o clock faz uma transição. Usado em contadores. 
  //   Um componente que pode ser inserido para gerar valores constantes (0 ou 1) que podem ser usados em diferentes partes do circuito.
  //   Probes são ferramentas de depuração que mostram o valor atual de um fio. Eles ajudam a visualizar se o sinal no fio é 0, 1, indefinido (X), ou de alta impedância (Z).
  //   Splitters são usados para dividir ou combinar fios que transportam múltiplos bits. Eles são úteis quando você quer manipular parte de um barramento ou combinar várias saídas em um único sinal.
  //   A cada combinação binária aplicada nas entradas, uma linha correspondente de saída é ativada. Ou seja, ele “decodifica” o valor de entrada para acionar uma linha única de saída.
  //   é um tipo de encoder (codificador) que converte várias entradas em um código binário, mas dá prioridade a uma entrada específica, caso múltiplas entradas sejam ativas ao mesmo tempo. Ele sempre codifica a entrada de maior prioridade.
  //   é um circuito combinacional que seleciona um de vários sinais de entrada e o direciona para uma única saída. Ele atua como um "selecionador" de sinal, permitindo que apenas uma das entradas seja transmitida para a saída com base em um conjunto de sinais de controle.
  //   Tem duas entradas (S e R). O estado do flip-flop pode ser "setado" (S = 1) ou "resetado" (R = 1).
  //   Tunnels permitem conectar diferentes partes do circuito sem a necessidade de desenhar fios longos. Eles funcionam como atalhos ou "túneis" através do qual os sinais são transmitidos de um lugar para outro no circuito. Cada túnel tem um nome, e todos os túneis com o mesmo nome estão conectados eletricamente.
  //   Armazena o valor presente na entrada D quando o clock faz uma transição (bordo de subida ou descida). É amplamente usado em registradores e memórias.
  //   É uma variação do SR, mas resolve o problema da condição indefinida. Quando J e K são ambos 1, ele inverte o estado.
endmodule
